# Fritzing sketch fanControl (saved by Fritzing 0.9.0b)
breadboards: 1

parts:
  S1 = Pushbutton [package="[THT]"]
  R1 = Resistor [tolerance=±5% resistance=220 package=THT]
  Part1 = Arduino Uno (Rev3)
  J1 = Basic Servo

nets (from the schematic view):
  N1: S1.Pin_1, R1.Pin_1, Part1.D2
  5V: S1.Pin_3, Part1.5V, J1.vcc
  GND: R1.Pin_0, Part1.GND, J1.gnd
  N2: Part1.D9_PWM, J1.pulse
